# Fritzing sketch vario_MS5611_pro (saved by Fritzing 0.9.3b)

parts:
  BMP1 = MS5611
  Composant3 = Bluetooth HC-05 Macho
  Composant2 = Arduino Nano (Rev3.0) (ICSP)

nets:
  VIN: BMP1.VIN, Composant3.VCC, Composant2.5V
  N1: BMP1.SCL, Composant2.A5
  N2: BMP1.SDA, Composant2.A4
  GND: BMP1.GND, Composant3.GND, Composant2.GND
  N3: Composant3.RXD, Composant2.D12/MISO

notes:
  ms5611
